# Fritzing sketch alon_rx (saved by Fritzing 0.9.5d)

parts:
  M1 = DOIT Esp32 DevKit v1 (30 pins long, 11 pins width) [part_number=ESP32S-PIN30]
  LCD2004-I2C1 = LCD2004-I2C
  M2 = Osoyoo SX1278-ra-02

nets:
  3V3: M1.3V3, M2.3.3V
  GND: M1.GND, LCD2004-I2C1.GND, M2.GND
  N1: M1.D5, M2.NSS
  N2: M1.D18, M2.SCK
  N3: M1.D19, M2.MISO
  N4: M1.D21, LCD2004-I2C1.SDA
  N5: M1.D22, LCD2004-I2C1.SCL
  N6: M1.D23, M2.MOSI
  N7: M1.D32, M2.RST
  N8: M1.D33, M2.DIO0
  VIN: M1.VIN, LCD2004-I2C1.VCC

notes:
  SX1278
  LoRa Module
  20x4
  IIC LCD
  ESP32
  Microcontroller

custom parts:
  DOIT Esp32 DevKit v1 (30 pins long, 11 pins width): The DOIT Esp32 DevKit v1 is one of the development board created by DOIT to evaluate the ESP-WROOM-32 module. It is based on the ESP32 microcontroller that boasts Wifi, Bluetooth, Ethernet and Low Power support all in a single chip. (vanepp) made breadboard work, adjusted pin numbering and labels and reduced size of schematic and cleaned up pcb. This chip is 30pins long (2 x15) and 11 pins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
  LCD2004-I2C: A standard character display with 4x20 characters. Comes in many colors with LCM2004 IIC attached.
  Osoyoo SX1278-ra-02: Osoyoo Long Distance wireless transceiver Uart LoRa Module.
