# Fritzing sketch alon_tx (saved by Fritzing 0.9.5d)

parts:
  M1 = DOIT Esp32 DevKit v1 (30 pins long, 11 pins width) [part_number=ESP32S-PIN30]
  M2 = Osoyoo SX1278-ra-02
  Driver2 = 28BYJ-48 Driver Module [part_number=ULN2003 package=THT]
  SM2 = 28BYJ-48 Stepper Motor [part_number=28BYJ-48]
  M3 = JSN-SRO4T [package=THT]

nets:
  3V3: M1.3V3, M2.3.3V
  GND: M1.GND, M2.GND, Driver2.GND, M3.pin1
  N1: M1.D5, M2.NSS
  N2: M1.D18, M2.SCK
  N3: M1.D19, M2.MISO
  N4: M1.D21, M3.pin3
  N5: M1.D22, M3.pin2
  N6: M1.D23, M2.MOSI
  N7: M1.D32, M2.RST
  N8: M1.D33, M2.DIO0
  N9: M1.VIN, Driver2.Vmotor, M3.pin4
  N10: Driver2.blue-pin, SM2.blue-pin
  N11: Driver2.pink-pin, SM2.pink-pin
  N12: Driver2.yellow-pin, SM2.yellow-pin
  N13: Driver2.orange-pin, SM2.orange-pin
  N14: Driver2.red-pin, SM2.red-pin

notes:
  JSN-SR04T
  Ultrasonic sensor
  SX1278
  LoRa module
  ULN2003
  5v Stepper Motor Driver
  28BYJ-48
  5v Stepper Motor
  ESP32
  Microcontroller

custom parts:
  DOIT Esp32 DevKit v1 (30 pins long, 11 pins width): The DOIT Esp32 DevKit v1 is one of the development board created by DOIT to evaluate the ESP-WROOM-32 module. It is based on the ESP32 microcontroller that boasts Wifi, Bluetooth, Ethernet and Low Power support all in a single chip. (vanepp) made breadboard work, adjusted pin numbering and labels and reduced size of schematic and cleaned up pcb. This chip is 30pins long (2 x15) and 11 pins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
  Osoyoo SX1278-ra-02: Osoyoo Long Distance wireless transceiver Uart LoRa Module.
  28BYJ-48 Driver Module: Generic male header
  28BYJ-48 Stepper Motor: Unipolar Stepper Motor 28BYJ-48 Top coil - pink & orange Bottom coil - blue & yellow Common rail - red Connector pins: blue - pink - yellow - orange - red
  JSN-SRO4T: JSN-SR04T Waterproof Ultrasonic Distance Measuring Module Integrated Ultrasonic Detection Module DC 5V.
